// Logisim project tp2_v2.circ as structural Verilog: 1 circuit, main circuit main
module main (
  input  ENB,
  input  A,
  input  B,
  input  C,
  input  Entrada
);

  wire nand_1_out, nand_2_out, nand_3_out, nand_4_out, nand_5_out, nand_6_out, nand_7_out, nand_8_out,
       nand_9_out, not_1_out, not_2_out, not_3_out, not_4_out, not_5_out, not_6_out, not_7_out, not_8_out,
       not_9_out, not_10_out, not_11_out, not_12_out, not_13_out, not_14_out, not_15_out;

  not not_1 (not_1_out, ENB);
  not not_2 (not_2_out, A);
  not not_3 (not_3_out, B);
  not not_4 (not_4_out, C);
  not not_5 (not_5_out, A);
  not not_6 (not_6_out, B);
  not not_7 (not_7_out, B);
  not not_8 (not_8_out, C);
  not not_9 (not_9_out, Entrada);
  not not_10 (not_10_out, Entrada);
  not not_11 (not_11_out, Entrada);
  not not_12 (not_12_out, Entrada);
  not not_13 (not_13_out, Entrada);
  not not_14 (not_14_out, Entrada);
  nand nand_1 (nand_1_out, not_2_out, not_3_out, not_4_out, not_1_out);
  nand nand_2 (nand_2_out, not_5_out, not_6_out, C, not_1_out);
  nand nand_3 (nand_3_out, A, B, C, not_1_out);
  nand nand_4 (nand_4_out, A, B, C, not_1_out);
  nand nand_5 (nand_5_out, A, not_7_out, C, not_1_out);
  nand nand_6 (nand_6_out, A, B, C, not_1_out);
  nand nand_7 (nand_7_out, A, B, not_8_out, not_1_out);
  nand nand_8 (nand_8_out, A, B, C, not_1_out);
  nand nand_9 (nand_9_out, nand_1_out, nand_2_out, nand_3_out, nand_4_out, nand_5_out, nand_6_out, nand_7_out, nand_8_out);
  not not_15 (not_15_out, nand_9_out);
  LED led_1 (.in(not_15_out));

  // Notes on the sheet:
  //   000
  //   001
  //   010
  //   011
  //   100
  //   101
  //   110
  //   111
endmodule
