// Logisim project tp2.circ as structural Verilog: 1 circuit, main circuit main
module main (
  input  ENB,
  input  A,
  input  B,
  input  C,
  input  Entrada
);

  wire and_1_out, and_2_out, and_3_out, and_4_out, and_5_out, and_6_out, and_7_out, and_8_out, not_1_out,
       not_2_out, not_3_out, not_4_out, not_5_out, not_6_out, not_7_out, not_8_out, not_9_out, not_10_out,
       not_11_out, not_12_out, not_13_out, not_14_out, or_1_out;

  not not_1 (not_1_out, ENB);
  not not_2 (not_2_out, A);
  not not_3 (not_3_out, B);
  not not_4 (not_4_out, C);
  not not_5 (not_5_out, A);
  not not_6 (not_6_out, B);
  not not_7 (not_7_out, B);
  not not_8 (not_8_out, C);
  not not_9 (not_9_out, Entrada);
  not not_10 (not_10_out, Entrada);
  not not_11 (not_11_out, Entrada);
  not not_12 (not_12_out, Entrada);
  not not_13 (not_13_out, Entrada);
  not not_14 (not_14_out, Entrada);
  and and_1 (and_1_out, not_2_out, not_3_out, not_9_out, not_4_out, not_1_out);
  and and_2 (and_2_out, not_5_out, not_6_out, not_10_out, C, not_1_out);
  and and_3 (and_3_out, A, B, not_11_out, C, not_1_out);
  and and_4 (and_4_out, A, B, not_12_out, C, not_1_out);
  and and_5 (and_5_out, A, not_7_out, not_13_out, C, not_1_out);
  and and_6 (and_6_out, A, B, not_14_out, C, not_1_out);
  and and_7 (and_7_out, A, B, Entrada, not_8_out, not_1_out);
  and and_8 (and_8_out, A, B, Entrada, C, not_1_out);
  or or_1 (or_1_out, and_1_out, and_2_out, and_3_out, and_4_out, and_5_out, and_6_out, and_7_out, and_8_out);
  LED led_1 (.in(or_1_out));

  // Notes on the sheet:
  //   000
  //   001
  //   010
  //   011
  //   100
  //   101
  //   110
  //   111
endmodule
