// Logisim project exercicio_7.circ as structural Verilog: 1 circuit, main circuit main
module main (
  input  in_1,
  input  in_2,
  input  in_3
);

  wire clock_1_out, d_ff_1_q, d_ff_1_qn, d_ff_2_q, d_ff_2_qn;

  Clock clock_1 (.out(clock_1_out));
  D_Flip_Flop d_ff_1 (.D(d_ff_1_qn), .clk(clock_1_out), .Q(d_ff_1_q), .Qn(d_ff_1_qn), .preset(in_1), .reset(in_3));
  LED led_1 (.in(d_ff_1_q));
  D_Flip_Flop d_ff_2 (.D(d_ff_2_qn), .clk(clock_1_out), .Q(d_ff_2_q), .Qn(d_ff_2_qn), .preset(in_2), .reset(in_3));
  LED led_2 (.in(d_ff_2_q));
endmodule
